// Logisim project IA39mips.circ as structural Verilog: 1 circuit, main circuit MIPS
module MIPS (
);

  wire addi, alu, clk, clock_1_out, FA, FPC, halt, lw, sw;
  wire [2:0] multiplexer_4_out;
  wire [3:0] control_alu_1_out;
  wire [4:0] rd, res_reg, rs, rt;
  wire [5:0] CODEOP, fn;
  wire [15:0] shift;
  wire [27:0] PC_4;
  wire [31:0] Ext32, IB, multiplexer_1_out, multiplexer_2_out, multiplexer_5_out, pc_1_pc, SalA, SalALU,
       SalB, SalMem;
  wire [31:2] DE_J;

  Clock #(.highDuration(10), .lowDuration(10)) clock_1 (.out(clock_1_out));
  Multiplexer #(.width(32), .enable("false")) multiplexer_1 (
    .in0({DE_J[31:28], PC_4}), .in1({DE_J, 2'b00}), .out(multiplexer_1_out), .sel(FPC));
  PC pc_1 (.IN(multiplexer_1_out), .PC(pc_1_pc), .clk(clk));
  // Probe on pc_1_pc
  and and_1 (halt, CODEOP[5], CODEOP[4], CODEOP[3], CODEOP[2], CODEOP[1], CODEOP[0]);
  ClockGen clockgen_1 (.halt(halt), .clkin(clock_1_out), .clkout(clk));
  Adder #(.width(32)) adder_1 (.a(32'h4), .b(pc_1_pc), .out({DE_J[31:28], PC_4}), .cin(1'b0));  // open: cout
  InstDecoder instdecoder_1 (
    .IB(IB), .IB31_26(CODEOP), .IB25_21(rs), .IB20_16(rt), .IB15_11(rd), .IB5_0(fn), .IB15_0(shift),
    .IB25_0(DE_J[27:2]));
  and and_2 (FPC, ~CODEOP[5], ~CODEOP[4], ~CODEOP[3], ~CODEOP[2], CODEOP[1], ~CODEOP[0]);  // AND_Gate
  Instruction_memory instruction_memory_1 (.Read_address(pc_1_pc), .Instruction(IB));
  and and_3 (lw, CODEOP[5], ~CODEOP[4], ~CODEOP[3], ~CODEOP[2], CODEOP[1], CODEOP[0]);  // AND_Gate
  // Probe on IB
  and and_4 (sw, CODEOP[5], ~CODEOP[4], CODEOP[3], ~CODEOP[2], CODEOP[1], CODEOP[0]);  // AND_Gate
  Multiplexer #(.width(32), .enable("false")) multiplexer_2 (
    .in0(SalMem), .in1(SalALU), .out(multiplexer_2_out), .sel(alu));
  and and_5 (alu, ~CODEOP[5], ~CODEOP[4], ~CODEOP[3], ~CODEOP[2], ~CODEOP[1], ~CODEOP[0]);  // AND_Gate
  Multiplexer #(.width(5), .enable("false")) multiplexer_3 (.in0(rt), .in1(rd), .out(res_reg), .sel(alu));
  assign Ext32 = {{16{shift[15]}}, shift};  // Bit_Extender bit_extender_1
  and and_6 (addi, ~CODEOP[5], ~CODEOP[4], CODEOP[3], ~CODEOP[2], ~CODEOP[1], ~CODEOP[0]);  // AND_Gate
  Register_file register_file_1 (
    .Read_Register_1(rs), .Read_Register_2(rt), .Write_Register(res_reg), .Write_Data(multiplexer_2_out),
    .Read_Data_1(SalA), .Read_Data_2(SalB), .clk(clk), .Write(FA));
  Multiplexer #(.width(3), .enable("false")) multiplexer_4 (
    .in0(3'b000), .in1(3'b111), .out(multiplexer_4_out), .sel(alu));
  Multiplexer #(.width(32), .enable("false")) multiplexer_5 (
    .in0(Ext32), .in1(SalB), .out(multiplexer_5_out), .sel(alu));
  Control_ALU control_alu_1 (.OpALU(multiplexer_4_out), .funcion(fn), .OUT(control_alu_1_out));
  ALU alu_1 (.A(SalA), .B(multiplexer_5_out), .Result(SalALU), .Operation(control_alu_1_out));  // open: Z
  or or_1 (FA, lw, alu);
  Data_Memory_32 data_memory_32_1 (
    .Address(SalALU), .Write_Data(SalB), .Read_Data(SalMem), .Write(sw), .clk(clk), .Read(lw));

  // Other names for the same wires on the sheet: DIR[25:0] = DE_J[27:2]; PC_4[31:28] = DE_J[31:28]; j = FPC; RM = lw;
  //   WM = sw
endmodule
